// Logisim project NAND2Tetris.circ as structural Verilog: 7 circuits, main circuit ALU
module main (
  input  [15:0] in_1,
  input  [15:0] in_2,
  output out_3
);

  wire button_1_out;
  wire [15:0] undriven, undriven_2;

  Button button_1 (.out(button_1_out));
  // Probe on in_1[15:8]
  // Probe on in_1[7:0]
  // Probe on in_2[15:8]
  // Probe on in_2[7:0]
  // a_commands_test a_commands_test_1: pin names not known; wires that end beside it: button_1_out
  // Probe on undriven[15:8]
  // Probe on undriven_2[15:8]
  // Probe on undriven[7:0]
  // Probe on undriven_2[7:0]

  // Notes on the sheet:
  //   in_2: pull=down
  //   in_1: pull=down
endmodule

module ALU (
  input  [15:0] x,
  input  [15:0] y,
  input  zx,
  input  nx,
  input  zy,
  input  ny,
  input  f,
  input  no,
  output [15:0] out,
  output zr,
  output ng
);

  wire NO_t, NX_t, NY_t, ZX_t, ZY_t;
  wire [15:0] adder_1_out, and_1_out, and_2_out, and_3_out, multiplexer_1_out, multiplexer_2_out,
       multiplexer_3_out, multiplexer_4_out, multiplexer_5_out, not_6_out, not_7_out, not_8_out, not_9_out,
       not_10_out;

  not not_1 (ZX_t, zx);
  not not_2 (NX_t, nx);
  not not_3 (ZY_t, zy);
  not not_4 (NY_t, ny);
  not not_5 (NO_t, no);
  assign not_6_out = ~x;  // NOT_Gate not_6, 16 bits wide
  // Probe on not_6_out
  assign and_1_out = not_6_out & x;  // AND_Gate and_1, 16 bits wide
  // Probe on not_7_out
  assign not_7_out = ~y;  // NOT_Gate not_7, 16 bits wide
  assign and_2_out = not_7_out & y;  // AND_Gate and_2, 16 bits wide
  // Probe on multiplexer_1_out
  // Probe on and_1_out
  Multiplexer #(.width(16), .enable("false")) multiplexer_1 (
    .in0(and_1_out), .in1(x), .out(multiplexer_1_out), .sel(ZX_t));
  // Probe on and_2_out
  assign not_8_out = ~multiplexer_1_out;  // NOT_Gate not_8, 16 bits wide
  // Probe on multiplexer_2_out
  Multiplexer #(.width(16), .enable("false")) multiplexer_2 (
    .in0(and_2_out), .in1(y), .out(multiplexer_2_out), .sel(ZY_t));
  assign not_9_out = ~multiplexer_2_out;  // NOT_Gate not_9, 16 bits wide
  Multiplexer #(.width(16), .enable("false")) multiplexer_3 (
    .in0(not_8_out), .in1(multiplexer_1_out), .out(multiplexer_3_out), .sel(NX_t));
  Multiplexer #(.width(16), .enable("false")) multiplexer_4 (
    .in0(not_9_out), .in1(multiplexer_2_out), .out(multiplexer_4_out), .sel(NY_t));
  assign and_3_out = multiplexer_4_out & multiplexer_3_out;  // AND_Gate and_3, 16 bits wide
  Adder #(.width(16)) adder_1 (.a(multiplexer_4_out), .b(multiplexer_3_out), .out(adder_1_out));  // open: cin, cout
  Multiplexer #(.width(16), .enable("false")) multiplexer_5 (
    .in0(and_3_out), .in1(adder_1_out), .out(multiplexer_5_out), .sel(f));
  Comparator #(.width(16), .mode("unsigned")) comparator_1 (.a(out), .b({16{1'b0}}), .eq(zr));  // open: gt, lt
  BitSelector #(.width(16)) bitselector_1 (.in(out), .out(ng), .sel(4'b1111));
  assign not_10_out = ~multiplexer_5_out;  // NOT_Gate not_10, 16 bits wide
  Multiplexer #(.width(16), .enable("false")) multiplexer_6 (
    .in0(not_10_out), .in1(multiplexer_5_out), .out(out), .sel(NO_t));

  // Notes on the sheet:
  //   f: pull=down
  //   y: pull=down
  //   zy: pull=down
  //   no: pull=down
  //   x: pull=down
  //   nx: pull=down
  //   zx: pull=down
  //   ny: pull=down
endmodule

// ALU
module CPU (
  input  [15:0] inM,
  input  [15:0] instruction,
  input  reset,
  output [15:0] outM,
  output [14:0] addressM,
  output [14:0] PC,
  output writeM
);

  wire alu_1_ng, alu_1_zr, not_1_out, not_2_out, T, WA, WD, WPC;
  wire [15:0] D_q, multiplexer_1_out, multiplexer_2_out;
  wire [15:15] A_q, PC_q;

  Clock clock_1 (.out(T));
  not not_1 (not_1_out, instruction[15]);
  Multiplexer #(.width(16), .disabled(0), .enable("false")) multiplexer_1 (
    .in0(outM), .in1(instruction), .out(multiplexer_1_out), .sel(not_1_out));
  not not_2 (not_2_out, WPC);
  // Probe on {A_q[15], addressM}
  Register #(.width(16)) A (.D(multiplexer_1_out), .en(WA), .Q({A_q[15], addressM}), .clk(T), .clr(reset));
  Multiplexer #(.width(16), .disabled(0), .enable("false")) multiplexer_2 (
    .in0({A_q[15], addressM}), .in1(inM), .out(multiplexer_2_out), .sel(instruction[12]));
  Counter #(.width(16), .max('hffff), .ongoal("stay")) u_PC (
    .load(WPC), .D({A_q[15], addressM}), .count(not_2_out), .Q({PC_q[15], PC}), .clk(T), .clr(reset));  // open: carry
  and and_1 (writeM, instruction[3], instruction[15]);
  and and_2 (WD, instruction[4], instruction[15]);
  or or_1 (WA, instruction[5], ~instruction[15]);  // OR_Gate
  // Probe on outM
  // Probe on D_q
  Register #(.width(16)) D (.D(outM), .en(WD), .Q(D_q), .clk(T), .clr(reset));
  ALU alu_1 (
    .x(D_q), .y(multiplexer_2_out), .zx(instruction[11]), .nx(instruction[10]), .zy(instruction[9]),
    .ny(instruction[8]), .f(instruction[7]), .no(instruction[6]), .out(outM), .zr(alu_1_zr), .ng(alu_1_ng));
  JMP jmp_1 (.LTZ(instruction[2]), .GTZ(instruction[1]), .ZR(instruction[0]));  // open: EQZ, NG, WPC, bit1

  // Other names for the same wires on the sheet: GTZ = instruction[0]; EQZ = instruction[1]; LTZ = instruction[2];
  //   NO = instruction[6]; F = instruction[7]; NY = instruction[8]; ZY = instruction[9]; NX = instruction[10];
  //   ZX = instruction[11]; a = instruction[12]; bit1 = instruction[15]; M[15:0] = inM; R = reset; WM = writeM

  // Notes on the sheet:
  //   reset: pull=down
  //   instruction: pull=down
  //   inM: pull=down
  //   writeM: pull=down
endmodule

module a_commands_test (
  input  [15:0] in_1,
  input  [15:0] in_2
);

  wire [15:0] alu_1_out;

  // Probe on 6'b010101
  // Probe on in_1
  // Probe on in_2
  ALU alu_1 (
    .x(in_1), .y(in_2), .zx(1'b0), .nx(1'b1), .zy(1'b0), .ny(1'b1), .f(1'b0), .no(1'b1), .out(alu_1_out));  // open: zr, ng
  // Probe on alu_1_out
  // Probe on alu_1_out

  // Notes on the sheet:
  //   in_1: pull=down
  //   in_2: pull=down
  //   101010  - 0
  //   111111  -> 1
  //   111010  -> -1
  //   001100  -> D
  //   110000  -> A
  //   001101  -> ! D
  //   110001  -> ! A
  //   001111  -> - D
  //   110011  -> - A
  //   011111  -> D + 1
  //   110111  -> A + 1
  //   001110  -> D - 1
  //   110010  -> A - 1
  //   000010  -> D + A
  //   010011  -> D - A
  //   000111  -> A - D
  //   000000  -> A & D
  //   010101  -> A | D
endmodule

module Comp (
  input  [15:0] in_1
);

  wire button_1_out, clock_1_out, cpu_1_writem;
  wire [14:0] cpu_1_addressm, cpu_1_pc;
  wire [15:0] cpu_1_outm, ram_1_data, rom_1_data;

  ROM #(.addrWidth(15), .dataWidth(16)) rom_1 (.addr(cpu_1_pc), .data(rom_1_data));  // open: sel
  // Probe on in_1
  // Probe on rom_1_data
  // Probe on cpu_1_pc
  CPU cpu_1 (
    .inM(ram_1_data), .instruction(rom_1_data), .outM(cpu_1_outm), .writeM(cpu_1_writem),
    .addressM(cpu_1_addressm), .PC(cpu_1_pc), .reset(button_1_out));
  Button button_1 (.out(button_1_out));
  // Probe on cpu_1_outm
  // Probe on cpu_1_addressm
  Clock clock_1 (.out(clock_1_out));
  RAM #(.addrWidth(15), .dataWidth(16), .bus("separate")) ram_1 (
    .addr(cpu_1_addressm), .din(cpu_1_outm), .data(ram_1_data), .str(cpu_1_writem), .clk(clock_1_out),
    .clr(button_1_out));  // open: sel, ld

  // Notes on the sheet:
  //   contents of rom_1 (hex, n*v repeats v):
  //   1 ec10 2 e090 0 e308 2 ec10 4 e090 2 e308 c ec07
endmodule

module JMP (
  input  LTZ,
  input  EQZ,
  input  GTZ,
  input  NG,
  input  ZR,
  input  bit1,
  output WPC
);

  wire not_1_out, not_2_out, not_3_out, not_4_out, not_5_out, o1_out, o2_out, o3_out, o4_out, o5_out, o6_out,
       o7_out, o8_out, o9_out, o10_out;

  not not_1 (not_1_out, EQZ);
  not not_2 (not_2_out, GTZ);
  not not_3 (not_3_out, NG);
  and o1 (o1_out, not_1_out, not_2_out);
  and o2 (o2_out, GTZ, not_3_out);
  not not_4 (not_4_out, ZR);
  and o3 (o3_out, LTZ, NG);
  not not_5 (not_5_out, ZR);
  and o4 (o4_out, o1_out, NG);
  and o5 (o5_out, o2_out, not_4_out);
  and o6 (o6_out, EQZ, ZR);
  and o7 (o7_out, o3_out, not_5_out);
  or o8 (o8_out, o4_out, o5_out);
  or o9 (o9_out, o6_out, o7_out);
  or o10 (o10_out, o8_out, o9_out);
  and and_1 (WPC, o10_out, bit1);
endmodule

module CPU_test (
  input  [14:0] in_1
);

  wire [15:0] rom_1_data;

  ROM #(.addrWidth(15), .dataWidth(16)) rom_1 (.addr(in_1), .data(rom_1_data), .sel(1'b1));
  CPU cpu_1 (.instruction(rom_1_data));  // open: inM, outM, writeM, addressM, PC, reset

  // Notes on the sheet:
  //   contents of rom_1 (hex, n*v repeats v):
  //   1111 2222 3333 12*0 3333 33 14*0 3300
endmodule
