// Logisim project NAND2Tetris_CPU.circ as structural Verilog: 1 circuit, main circuit CPU
module CPU (
  input  [15:0] inM,
  input  [15:0] instruction,
  input  reset,
  output [15:0] outM,
  output writeM,
  output [14:0] addressM,
  output [14:0] pc
);

  wire TACK, TICK;
  wire [15:0] multiplexer_1_out;

  Clock clock_1 (.out(TICK));
  Multiplexer #(.width(16)) multiplexer_1 (
    .in0(inM), .in1(instruction), .out(multiplexer_1_out), .sel(instruction[15]));  // open: en
  Register #(.width(16)) A (.D(multiplexer_1_out), .clk(TACK));  // open: en, Q, clr
  Counter #(.width(16), .max('hffff)) u_PC ();  // open: load, D, count, Q, carry, clk, clr
  Register #(.width(16)) D ();  // open: D, en, Q, clk, clr
  Multiplexer #(.width(16)) multiplexer_2 ();  // open: in0, in1, out, sel, en
endmodule
